// Logisim project 16-1 MUX using 4-1 MUX.circ as structural Verilog: 1 circuit, main circuit main
module main (
  input  d0,
  input  d1,
  input  d2,
  input  d3,
  input  d4,
  input  d5,
  input  d6,
  input  d7,
  input  d8,
  input  d9,
  input  d10,
  input  [1:0] S3S2,
  input  d11,
  input  d12,
  input  d13,
  input  d14,
  input  d15,
  input  [1:0] S1S0
);

  wire multiplexer_1_out, multiplexer_2_out, multiplexer_3_out, multiplexer_4_out, multiplexer_5_out;

  Multiplexer #(.select(2)) multiplexer_1 (
    .in0(d0), .in1(d1), .in2(d2), .in3(d3), .out(multiplexer_1_out), .sel(S1S0));  // open: en
  Multiplexer #(.select(2)) multiplexer_2 (
    .in0(d4), .in1(d5), .in2(d6), .in3(d7), .out(multiplexer_2_out), .sel(S1S0));  // open: en
  Multiplexer #(.select(2)) multiplexer_3 (
    .in0(d8), .in1(d9), .in2(d10), .in3(d11), .out(multiplexer_3_out), .sel(S1S0));  // open: en
  Multiplexer #(.select(2)) multiplexer_4 (
    .in0(d12), .in1(d13), .in2(d14), .in3(d15), .out(multiplexer_4_out), .sel(S1S0));  // open: en
  Multiplexer #(.select(2)) multiplexer_5 (
    .in0(multiplexer_1_out), .in1(multiplexer_2_out), .in2(multiplexer_3_out), .in3(multiplexer_4_out),
    .out(multiplexer_5_out), .sel(S3S2));  // open: en
  LED led_1 (.in(multiplexer_5_out));

  // Notes on the sheet:
  //   16-to-1 MUX using 4-to-1 MUX
endmodule
