// Logisim project 7 Segment (Digital Digit 0-9 with Don_t Care).circ as structural Verilog: 1 circuit, main circuit main
module main (
  input  A,
  input  B,
  input  C,
  input  D
);

  wire and_1_out, and_2_out, and_3_out, and_4_out, and_5_out, and_6_out, and_7_out, not_1_out, not_2_out,
       not_3_out, or_1_out, or_2_out, or_3_out, or_4_out, or_5_out, or_6_out, or_7_out, or_8_out, or_9_out,
       xnor_1_out, xnor_2_out, xor_1_out;

  not not_1 (not_1_out, B);
  not not_2 (not_2_out, C);
  not not_3 (not_3_out, D);
  xnor xnor_1 (xnor_1_out, B, D);
  xnor xnor_2 (xnor_2_out, C, D);
  and and_1 (and_1_out, B, not_2_out, D);
  and and_2 (and_2_out, not_1_out, not_3_out);
  or or_1 (or_1_out, not_1_out, not_3_out);
  or or_2 (or_2_out, not_1_out, C);
  and and_3 (and_3_out, not_3_out, not_2_out);
  or or_3 (or_3_out, not_3_out, not_2_out);
  and and_4 (and_4_out, not_3_out, B);
  xor xor_1 (xor_1_out, B, C);
  and and_5 (and_5_out, or_1_out, C);
  and and_6 (and_6_out, or_3_out, B);
  or or_4 (or_4_out, xnor_1_out, A, C);
  or or_5 (or_5_out, not_1_out, xnor_2_out);
  or or_6 (or_6_out, B, not_2_out, D);
  or or_7 (or_7_out, and_1_out, and_2_out, and_5_out, A);
  and and_7 (and_7_out, not_3_out, or_2_out);
  or or_8 (or_8_out, and_3_out, and_6_out, A);
  or or_9 (or_9_out, and_4_out, xor_1_out, A);
  _7_Segment_Display u_7_segment_display_1 (
    .g(or_9_out), .f(or_8_out), .a(or_4_out), .b(or_5_out), .e(and_7_out), .d(or_7_out), .c(or_6_out));  // open: dp

  // Notes on the sheet:
  //   a
  //   b
  //   c
  //   d
  //   e
  //   f
  //   g
endmodule
