// Logisim project 7 Segment (Digital Digit).circ as structural Verilog: 1 circuit, main circuit 7 segment (0-F)
module _7_segment__0_F (
  input  W,
  input  X,
  input  Y,
  input  Z,
  output a,
  output b,
  output c,
  output d,
  output e,
  output f,
  output g
);

  wire and_1_out, and_2_out, and_3_out, and_4_out, and_5_out, nand_1_out, nand_2_out, nand_3_out, nand_4_out,
       nand_5_out, nand_6_out, nand_7_out, nand_8_out, nand_9_out, nand_10_out, nand_11_out, nand_12_out,
       nand_13_out, nand_14_out, nand_15_out, nand_16_out, nand_17_out, nand_18_out, nand_19_out,
       nand_20_out, nand_21_out, nand_22_out, nand_23_out, nand_24_out, nand_25_out, nand_26_out,
       nand_27_out, nand_28_out, nand_29_out, nand_30_out, nand_31_out, nand_32_out, nand_33_out,
       nand_34_out, nand_35_out, nand_36_out, nand_37_out, nand_38_out, nand_39_out, nand_40_out,
       nand_41_out, nand_42_out, nand_43_out, nand_44_out, nand_45_out, nand_46_out, nand_47_out,
       nand_48_out, nand_49_out, nand_50_out, nand_51_out, nand_52_out, nand_53_out, nand_54_out,
       nand_55_out, nand_56_out, nand_57_out, nand_58_out, nand_59_out, nand_60_out, nand_61_out,
       nand_62_out, nand_63_out, nand_64_out, nand_65_out, nand_66_out, nand_67_out, nand_68_out, not_1_out,
       not_2_out, not_3_out, not_4_out, not_5_out;

  nand nand_1 (nand_1_out, X, X);
  nand nand_2 (nand_2_out, Z, Z);
  nand nand_3 (nand_3_out, W, W);
  nand nand_4 (nand_4_out, W, W);
  nand nand_5 (nand_5_out, X, X);
  nand nand_6 (nand_6_out, Y, Y);
  nand nand_7 (nand_7_out, Z, Z);
  nand nand_8 (nand_8_out, W, W);
  nand nand_9 (nand_9_out, X, X);
  nand nand_10 (nand_10_out, W, W);
  nand nand_11 (nand_11_out, Y, Y);
  nand nand_12 (nand_12_out, Z, Z);
  nand nand_13 (nand_13_out, X, X);
  nand nand_14 (nand_14_out, Z, Z);
  nand nand_15 (nand_15_out, W, W);
  nand nand_16 (nand_16_out, Y, Y);
  nand nand_17 (nand_17_out, W, W);
  nand nand_18 (nand_18_out, Y, Y);
  nand nand_19 (nand_19_out, W, W);
  nand nand_20 (nand_20_out, Y, Y);
  nand nand_21 (nand_21_out, W, W);
  nand nand_22 (nand_22_out, X, X);
  nand nand_23 (nand_23_out, W, W);
  nand nand_24 (nand_24_out, X, X);
  nand nand_25 (nand_25_out, Z, Z);
  nand nand_26 (nand_26_out, X, X);
  nand nand_27 (nand_27_out, Y, Y);
  nand nand_28 (nand_28_out, Z, Z);
  nand nand_29 (nand_29_out, Y, Y);
  nand nand_30 (nand_30_out, X, X);
  nand nand_31 (nand_31_out, Z, Z);
  nand nand_32 (nand_32_out, Z, Z);
  nand nand_33 (nand_33_out, Y, Y);
  nand nand_34 (nand_34_out, Z, Z);
  nand nand_35 (nand_35_out, W, W);
  nand nand_36 (nand_36_out, Y, Y);
  nand nand_37 (nand_37_out, Z, Z);
  nand nand_38 (nand_38_out, X, X);
  not not_1 (not_1_out, X);
  and and_1 (and_1_out, not_1_out, Y);
  and and_2 (and_2_out, Y, not_2_out);
  not not_2 (not_2_out, Z);
  not not_3 (not_3_out, W);
  and and_3 (and_3_out, not_3_out, X, not_4_out);
  not not_4 (not_4_out, Y);
  and and_4 (and_4_out, W, not_5_out);
  not not_5 (not_5_out, X);
  and and_5 (and_5_out, W, Z);
  nand nand_39 (nand_39_out, nand_1_out, nand_2_out);
  nand nand_40 (nand_40_out, nand_3_out, Y);
  nand nand_41 (nand_41_out, nand_4_out, X, Z);
  nand nand_42 (nand_42_out, X, Y);
  nand nand_43 (nand_43_out, W, nand_5_out, nand_6_out);
  nand nand_44 (nand_44_out, W, nand_7_out);
  nand nand_45 (nand_45_out, nand_8_out, nand_9_out);
  nand nand_46 (nand_46_out, nand_10_out, nand_11_out, nand_12_out);
  nand nand_47 (nand_47_out, nand_13_out, nand_14_out);
  nand nand_48 (nand_48_out, nand_15_out, Y, Z);
  nand nand_49 (nand_49_out, W, nand_16_out, Z);
  nand nand_50 (nand_50_out, nand_17_out, nand_18_out);
  nand nand_51 (nand_51_out, nand_19_out, Z);
  nand nand_52 (nand_52_out, nand_20_out, Z);
  nand nand_53 (nand_53_out, nand_21_out, X);
  nand nand_54 (nand_54_out, W, nand_22_out);
  nand nand_55 (nand_55_out, nand_23_out, nand_24_out, nand_25_out);
  nand nand_56 (nand_56_out, nand_26_out, Y, Z);
  nand nand_57 (nand_57_out, X, nand_27_out, Z);
  nand nand_58 (nand_58_out, X, Y, nand_28_out);
  nand nand_59 (nand_59_out, W, nand_29_out);
  nand nand_60 (nand_60_out, nand_30_out, nand_31_out);
  nand nand_61 (nand_61_out, Y, nand_32_out);
  nand nand_62 (nand_62_out, W, Y);
  nand nand_63 (nand_63_out, W, X);
  nand nand_64 (nand_64_out, nand_33_out, nand_34_out);
  nand nand_65 (nand_65_out, nand_35_out, X, nand_36_out);
  nand nand_66 (nand_66_out, X, nand_37_out);
  nand nand_67 (nand_67_out, W, nand_38_out);
  nand nand_68 (nand_68_out, W, Y);
  or or_1 (g, and_1_out, and_2_out, and_3_out, and_4_out, and_5_out);
  nand nand_69 (a, nand_39_out, nand_40_out, nand_41_out, nand_42_out, nand_43_out, nand_44_out);
  nand nand_70 (b, nand_45_out, nand_46_out, nand_47_out, nand_48_out, nand_49_out);
  nand nand_71 (c, nand_50_out, nand_51_out, nand_52_out, nand_53_out, nand_54_out);
  nand nand_72 (d, nand_55_out, nand_56_out, nand_57_out, nand_58_out, nand_59_out);
  nand nand_73 (e, nand_60_out, nand_61_out, nand_62_out, nand_63_out);
  nand nand_74 (f, nand_64_out, nand_65_out, nand_66_out, nand_67_out, nand_68_out);
  _7_Segment_Display u_7_segment_display_1 (.g(g), .f(f), .a(a), .b(b), .e(e), .d(d), .c(c));  // open: dp
endmodule
