// Logisim project BCD Adder.circ as structural Verilog: 1 circuit, main circuit main
module main (
  input  B3,
  input  B2,
  input  B1,
  input  B0,
  input  A3,
  input  A2,
  input  A1,
  input  A0,
  input  Carry_in,
  input  user_library,
  input  Always_0,
  output Carry_Output,
  output C,
  output S8,
  output S4,
  output S2,
  output S1
);

  wire and_1_out, and_2_out, main_1_c3, main_1_s0, main_1_s1, main_1_s2, main_1_s3;

  or or_1 (Carry_Output, main_1_c3, and_1_out, and_2_out);
  and and_1 (and_1_out, main_1_s3, main_1_s2);
  and and_2 (and_2_out, main_1_s3, main_1_s1);
  _4_bit_Binary_Adder__User_Library__main main_1 (
    .C3(main_1_c3), .B3(B3), .A3(A3), .B2(B2), .A2(A2), .B1(B1), .A1(A1), .B0(B0), .A0(A0), .C(Carry_in),
    .S3(main_1_s3), .S2(main_1_s2), .S1(main_1_s1), .S0(main_1_s0));
  _4_bit_Binary_Adder__User_Library__main main_2 (
    .C3(C), .B3(Always_0), .A3(main_1_s3), .B2(Carry_Output), .A2(main_1_s2), .B1(Carry_Output),
    .A1(main_1_s1), .B0(Always_0), .A0(main_1_s0), .C(user_library), .S3(S8), .S2(S4), .S1(S2), .S0(S1));

  // Notes on the sheet:
  //   BCD Adder
  //   0   1   1   0
  //   B3          B0
  //   Addend
  //   Z8
  //   Augend
  //   Z1
  //   Z2
  //   Z4
  //   Always 0
  //   according to
endmodule
