// Logisim project Full Adder using Decoder (3 input).circ as structural Verilog: 1 circuit, main circuit main
module main (
  input  E,
  input  A,
  input  B,
  input  C,
  output Sum,
  output Carry
);

  wire and_1_out, and_2_out, and_3_out, and_4_out, and_5_out, and_6_out, and_7_out, and_8_out, not_1_out,
       not_2_out, not_3_out;

  not not_1 (not_1_out, A);
  not not_2 (not_2_out, B);
  not not_3 (not_3_out, C);
  and and_1 (and_1_out, not_1_out, not_2_out, not_3_out, E);
  and and_2 (and_2_out, not_1_out, not_2_out, C, E);
  and and_3 (and_3_out, not_1_out, B, not_3_out, E);
  and and_4 (and_4_out, not_1_out, B, C, E);
  and and_5 (and_5_out, A, not_2_out, not_3_out, E);
  and and_6 (and_6_out, A, not_2_out, C, E);
  and and_7 (and_7_out, A, B, not_3_out, E);
  and and_8 (and_8_out, A, B, C, E);
  or or_1 (Sum, and_2_out, and_3_out, and_5_out, and_8_out);
  or or_2 (Carry, and_4_out, and_6_out, and_7_out, and_8_out);

  // Notes on the sheet:
  //   d3
  //   d4
  //   d5
  //   d0
  //   d1
  //   d2
  //   d6
  //   d7
  //   Sum (1, 2, 4, 7)
  //   Carry (3, 5, 6, 7)
endmodule
