// Logisim project Multiplier (2 bit).circ as structural Verilog: 1 circuit, main circuit main
module main (
  input  B1,
  input  B0,
  input  A1,
  input  A0,
  output out_5,
  output out_6,
  output out_7,
  output out_8
);

  wire and_2_out, and_3_out, and_4_out, main_1_carry;

  and and_1 (out_8, A0, B0);
  and and_2 (and_2_out, A1, B0);
  and and_3 (and_3_out, A0, B1);
  and and_4 (and_4_out, A1, B1);
  Half_Adder__User_Library__main main_1 (.A(and_2_out), .B(and_3_out), .Sum(out_7), .Carry(main_1_carry));
  Half_Adder__User_Library__main main_2 (.A(main_1_carry), .B(and_4_out), .Sum(out_6), .Carry(out_5));

  // Notes on the sheet:
  //   A0B0
  //   A1B0
  //   A0B1
  //   A1B1
  //   HA1
  //   C1
  //   HA2
  //   C2
  //   P3
  //   P2
  //   P1
  //   P0
endmodule
