// Logisim project Priority Encoder (4 by 2).circ as structural Verilog: 1 circuit, main circuit main
module main (
  input  I3,
  input  I2,
  input  I1,
  input  I0,
  input  I0_2,
  input  I1_2,
  input  I2_2,
  input  I3_2,
  output out_9,
  output Y1,
  output [1:0] Y1Y0,
  output out_12
);

  wire and_1_out, not_1_out;

  not not_1 (not_1_out, I2);
  and and_1 (and_1_out, I1, not_1_out);
  Priority_Encoder #(.select(2)) priority_encoder_1 (
    .in0(I0_2), .in1(I1_2), .in2(I2_2), .in3(I3_2), .out(Y1Y0), .gs(out_12));  // open: en_out, en_in
  or or_1 (out_9, and_1_out, I3);
  or or_2 (Y1, I2, I3);

  // Notes on the sheet:
  //   Y0
endmodule
