// Logisim project Full Adder 3 input (User Library).circ as structural Verilog: 1 circuit, main circuit main
module main (
  input  A,
  input  B,
  input  C_in,
  output out_4,
  output out_5
);

  wire and_1_out, and_2_out, xor_1_out;

  xor xor_1 (xor_1_out, A, B);
  and and_1 (and_1_out, C_in, xor_1_out);
  and and_2 (and_2_out, A, B);
  xor xor_2 (out_4, xor_1_out, C_in);
  or or_1 (out_5, and_1_out, and_2_out);

  // Notes on the sheet:
  //   Sum
  //   Carry
endmodule
